# Fritzing sketch Soilbuddy (saved by Fritzing 0.9.3b)
breadboards: 1

parts:
  Part1 = Photon
  M2 = DC Motor
  R1 = Resistor [tolerance=±5% resistance=1k package="1206 [SMD]"]
  Part2 = Soil Moisture Sensor
  D1 = Diode [package=diode-1n4148]
  Q1 = NPN-Transistor [part_number=BC337 package="TO92 [THT]"]

nets:
  N1: Part1.A3, Part2.SIG
  N2: Part1.A4, Part2.VCC
  N3: Part1.GND, Q1.C
  N4: Part1.D4, R1.Pin_1
  N5: Part1.3V3, M2.pin_2, D1.C
  N6: M2.pin_1, D1.A, Q1.E
  N7: R1.Pin_0, Q1.B
